# Fritzing sketch Temperature Sensor (saved by Fritzing 0.9.3b)

parts:
  Part1 = Adafruit Feather M0 RFM9x LoRa [part_number="Adafruit #3178 or #3179"]
  DS1 = DS18B20 1-Wire Temperature Sensor [part_number=DS18B20]
  R1 = Resistor [tolerance=±5% resistance=4.7k package="2512 [SMD]"]

nets:
  N1: Part1.DIO1, Part1.D5
  GND: Part1.GND, DS1.GND
  N2: Part1.D11, DS1.DQ, R1.Pin_1
  N3: Part1.D10, DS1.VDD, R1.Pin_0
  N4: Part1.D6, Part1.DIO2

custom parts:
  Adafruit Feather M0 RFM9x LoRa: This is the Adafruit Feather M0 RFM95 LoRa Radio - our take on an microcontroller with a "Long Range (LoRa)" packet radio transceiver with built in USB and battery charging. Its an Adafruit Feather M0 with a 433Mhz or 900MHz radio module cooked in! Great for making wireless networks that are more flexible than Bluetooth LE and without the high power requirements of WiFi. We have other boards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
